// Logisim project Lab10_Counter.circ as structural Verilog: 1 circuit, main circuit main
module main (
  input  M
);

  wire A_q, and_1_out, and_2_out, and_3_out, and_4_out, B_q, B_qn, C_q, C_qn, clock_1_out, not_1_out,
       or_1_out, or_2_out;

  Clock clock_1 (.out(clock_1_out));
  not not_1 (not_1_out, M);
  T_Flip_Flop C (.clk(clock_1_out), .T(1'b1), .Q(C_q), .Qn(C_qn));  // open: preset, reset, en
  and and_1 (and_1_out, not_1_out, C_q);
  and and_2 (and_2_out, M, C_qn);
  or or_1 (or_1_out, and_1_out, and_2_out);
  T_Flip_Flop B (.clk(clock_1_out), .T(or_1_out), .Q(B_q), .Qn(B_qn));  // open: preset, reset, en
  and and_3 (and_3_out, and_1_out, B_q);
  and and_4 (and_4_out, B_qn, and_2_out);
  or or_2 (or_2_out, and_3_out, and_4_out);
  T_Flip_Flop A (.clk(clock_1_out), .T(or_2_out), .Q(A_q));  // open: Qn, preset, reset, en
endmodule
